# Fritzing sketch drumduino (saved by Fritzing 0.9.2b)
breadboards: 2

parts:
  R1 = Resistor [tolerance=±5% resistance=1M package=THT]
  TX_SWITCH = male pin header, 3 pins [form="♂ (male)"]
  RX_SWITCH = male alternating pin header, 3 pins [form="♂ (male)"]
  MIDI_IN = DIN-5 jack (MIDI) [package=THT]
  MIDI_THRU = DIN-5 jack (MIDI) [package=THT]
  MIDI_OUT = DIN-5 jack (MIDI) [package=THT]
  R2 = Resistor [tolerance=±5% resistance=1M package=THT]
  R4 = Resistor [tolerance=±5% resistance=1M package=THT]
  R5 = Resistor [tolerance=±5% resistance=1M package=THT]
  R6 = Resistor [tolerance=±5% resistance=1M package=THT]
  LCD1 = LCD screen [part_number=hd44780]
  R7 = Trimmer Potentiometer [maximum_resistance=10kΩ package=THT]
  IC7 = 6N139 [chip_label=6N139 package="DIP (Dual Inline) [THT]"]
  R8 = Resistor [tolerance=±5% resistance=220 package=THT]
  R9 = Resistor [tolerance=±5% resistance=3.3k package=THT]
  D1 = 1N4148 [part_number=1N4148 package="300 mil [THT]"]
  IC8 = 74HC4851N [chip_label="74HC4851N " package="DIP (Dual Inline) [THT]"]
  IC9 = 74HC4851N [chip_label="74HC4851N " package="DIP (Dual Inline) [THT]"]
  IC10 = 74HC4851N [chip_label="74HC4851N " package="DIP (Dual Inline) [THT]"]
  IC11 = 74HC4851N [chip_label="74HC4851N " package="DIP (Dual Inline) [THT]"]
  IC12 = 74HC4851N [chip_label="74HC4851N " package="DIP (Dual Inline) [THT]"]
  IC13 = 74HC4851N [chip_label="74HC4851N " package="DIP (Dual Inline) [THT]"]
  R3 = Resistor [tolerance=±5% resistance=1M package=THT]
  IC14 = DIP - 14 pins [chip_label=SN54HC0 package="DIP (Dual Inline) [THT]"]
  R10 = Resistor [tolerance=±5% resistance=220 package=THT]
  R11 = Resistor [tolerance=±5% resistance=220 package=THT]
  R12 = Resistor [tolerance=±5% resistance=220 package=THT]
  R13 = Resistor [tolerance=±5% resistance=220 package=THT]
  R14 = Resistor [tolerance=±5% resistance=120 package=THT]
  RST_SW = Toggle Switch [package=THT]
  PWR_LED = LED - 5mm [color="Red (633nm)" package="5 mm [THT]"]
  R15 = Resistor [tolerance=±5% resistance=120 package=THT]
  BTN_LEFT = Pushbutton [package=THT]
  BTN_RIGHT = Pushbutton [package=THT]
  BTN_UP = Pushbutton [package=THT]
  BTN_DOWN = Pushbutton [package=THT]
  BTN_ESC = Pushbutton [package=THT]
  BTN_OK = Pushbutton [package=THT]
  Bauteil1 = Arduino Nano (Rev3.0)
  J1 = shrouded pin header, 10 pins [form="♂ (shrouded male)"]
  J2 = shrouded pin header, 10 pins [form="♂ (shrouded male)"]
  J3 = shrouded pin header, 10 pins [form="♂ (shrouded male)"]
  J4 = shrouded pin header, 10 pins [form="♂ (shrouded male)"]
  J5 = shrouded pin header, 10 pins [form="♂ (shrouded male)"]
  J6 = shrouded pin header, 10 pins [form="♂ (shrouded male)"]

nets:
  AD_0: R1.Pin_0, IC8.COM, Bauteil1.A0
  GND: R1.Pin_1, MIDI_IN.GND, MIDI_THRU.2, MIDI_THRU.GND, MIDI_OUT.2, MIDI_OUT.GND, R2.Pin_1, R4.Pin_1, R5.Pin_1, R6.Pin_1, LCD1.VSS, LCD1.R/W, LCD1.LED-, R7.leg1, IC7.GND, IC8.INH, IC8.GND, IC9.INH, IC9.GND, IC10.INH, IC10.GND, IC11.INH, IC11.GND, IC12.INH, IC12.GND, IC13.INH, IC13.GND, R3.Pin_1, IC14.GND, RST_SW.L2, PWR_LED.cathode, BTN_LEFT.leg1, BTN_RIGHT.leg1, BTN_UP.leg1, BTN_DOWN.leg1, BTN_ESC.leg1, BTN_OK.leg1, Bauteil1.GND, J1.pin10, J2.pin10, J3.pin10, J4.pin10, J5.pin10, J6.pin10
  ARDUINO_TX: TX_SWITCH.pin1, Bauteil1.D1/TX
  TX: TX_SWITCH.pin2, IC14.2A
  SOFTSERIAL_TX: TX_SWITCH.pin3, Bauteil1.D3
  ARDUINO_RX: RX_SWITCH.pin1, Bauteil1.D0/RX
  RX: RX_SWITCH.pin2, IC7.VO, R9.Pin_1, IC14.5A
  SOFTSERIAL_RX: RX_SWITCH.pin3, Bauteil1.D2
  N1: MIDI_IN.5, IC7.Vf-, D1.anode
  N2: MIDI_IN.4, R8.Pin_0
  N3: MIDI_THRU.5, R13.Pin_1
  N4: MIDI_THRU.4, R12.Pin_1
  N5: MIDI_OUT.5, R10.Pin_1
  N6: MIDI_OUT.4, R11.Pin_1
  AD_1: R2.Pin_0, IC9.COM, Bauteil1.A1
  AD_3: R4.Pin_0, IC11.COM, Bauteil1.A3
  AD_4: R5.Pin_0, IC12.COM, Bauteil1.A4
  AD_5: R6.Pin_0, IC13.COM, Bauteil1.A5
  5V: LCD1.VDD, LCD1.LED+, R7.wiper, IC7.VCC, R9.Pin_0, IC8.VCC, IC9.VCC, IC10.VCC, IC11.VCC, IC12.VCC, IC13.VCC, IC14.Vcc, R11.Pin_0, R12.Pin_0, R14.Pin_0, Bauteil1.5V, J1.pin1, J2.pin1, J3.pin1, J4.pin1, J5.pin1, J6.pin1
  LCD_INTENSITY: LCD1.V0, R7.leg2
  LCD_RS: LCD1.RS
  LCD_E: LCD1.E
  LCD_DB4: LCD1.DB4
  LCD_DB5: LCD1.DB5
  LCD_DB6: LCD1.DB6
  LCD_DB7: LCD1.DB7
  N7: IC7.Vf+, R8.Pin_1, D1.cathode
  PORT_A_4: IC8.Y4, J1.pin6
  PORT_A_6: IC8.Y6, J1.pin8
  PORT_A_7: IC8.Y7, J1.pin9
  PORT_A_5: IC8.Y5, J1.pin7
  DMUX_C: IC8.C, IC9.C, IC10.C, IC11.C, IC12.C, IC13.C, Bauteil1.D6
  DMUX_B: IC8.B, IC9.B, IC10.B, IC11.B, IC12.B, IC13.B, Bauteil1.D5
  DMUX_A: IC8.A, IC9.A, IC10.A, IC11.A, IC12.A, IC13.A, Bauteil1.D4
  PORT_A_3: IC8.Y3, J1.pin5
  PORT_A_0: IC8.Y0, J1.pin2
  PORT_A_1: IC8.Y1, J1.pin3
  PORT_A_2: IC8.Y2, J1.pin4
  PORT_B_4: IC9.Y4, J2.pin6
  PORT_B_6: IC9.Y6, J2.pin8
  PORT_B_7: IC9.Y7, J2.pin9
  PORT_B_5: IC9.Y5, J2.pin7
  PORT_B_3: IC9.Y3, J2.pin5
  PORT_B_0: IC9.Y0, J2.pin2
  PORT_B_1: IC9.Y1, J2.pin3
  PORT_B_2: IC9.Y2, J2.pin4
  PORT_C_4: IC10.Y4, J3.pin6
  PORT_C_6: IC10.Y6, J3.pin8
  AD_2: IC10.COM, R3.Pin_0, Bauteil1.A2
  PORT_C_7: IC10.Y7, J3.pin9
  PORT_C_5: IC10.Y5, J3.pin7
  PORT_C_3: IC10.Y3, J3.pin5
  PORT_C_0: IC10.Y0, J3.pin2
  PORT_C_1: IC10.Y1, J3.pin3
  PORT_C_2: IC10.Y2, J3.pin4
  PORT_D_4: IC11.Y4, J4.pin6
  PORT_D_6: IC11.Y6, J4.pin8
  PORT_D_7: IC11.Y7, J4.pin9
  PORT_D_5: IC11.Y5, J4.pin7
  PORT_D_3: IC11.Y3, J4.pin5
  PORT_D_0: IC11.Y0, J4.pin2
  PORT_D_1: IC11.Y1, J4.pin3
  PORT_D_2: IC11.Y2, J4.pin4
  PORT_E_4: IC12.Y4, J5.pin6
  PORT_E_6: IC12.Y6, J5.pin8
  PORT_E_7: IC12.Y7, J5.pin9
  PORT_E_5: IC12.Y5, J5.pin7
  PORT_E_3: IC12.Y3, J5.pin5
  PORT_E_0: IC12.Y0, J5.pin2
  PORT_E_1: IC12.Y1, J5.pin3
  PORT_E_2: IC12.Y2, J5.pin4
  PORT_F_4: IC13.Y4, J6.pin6
  PORT_F_6: IC13.Y6, J6.pin8
  PORT_F_7: IC13.Y7, J6.pin9
  PORT_F_5: IC13.Y5, J6.pin7
  PORT_F_3: IC13.Y3, J6.pin5
  PORT_F_0: IC13.Y0, J6.pin2
  PORT_F_1: IC13.Y1, J6.pin3
  PORT_F_2: IC13.Y2, J6.pin4
  N8: IC14.2Y, IC14.3A
  N9: IC14.3Y, R10.Pin_0
  N10: IC14.4Y, R13.Pin_0
  N11: IC14.4A, IC14.5Y
  N12: R14.Pin_1, RST_SW.L1
  RESET: RST_SW.COM, Bauteil1.RESET
  N13: PWR_LED.anode, R15.Pin_0
  3.3V: R15.Pin_1, Bauteil1.3V3
  BTN_L: BTN_LEFT.leg0
  BTN_R: BTN_RIGHT.leg0
  BTN_U: BTN_UP.leg0
  BTN_D: BTN_DOWN.leg0
  BTN_ESC: BTN_ESC.leg0
  BTN_OK: BTN_OK.leg0

custom parts:
  6N139: DARLINGTON OPTOCOUPLERS The 6N138/9 and HCPL-2730/HCPL-2731 optocouplers consist of an AlGaAs LED optically coupled to a high gain split darlington photodetector. The split darlington configuration separating the input photodiode and the first stage gain from the output transistor permits lower output saturation voltage and higher speed operation than possible with conventional darlington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
  1N4148: Small Signal Fast Switching Diode
  74HC4851N: 8-Channel Analog Multiplexer/Demultiplexer with Injection-Current Effect Control
  DIP - 14 pins: A DIP stand-in part for whatever IC you want. With 14 pins on a 300mil dual inline package (DIP) footprint.

// code stored in the sketch: drumduino_firmware.ino
#include <SoftwareSerial.h>

#define USE_DISPLAY 1

#if USE_DISPLAY
#include <LiquidCrystal.h>
LiquidCrystal lcd(7, 8, 9, 10, 11, 12);
#endif


enum DrumduinoFirmwareSettings {
	PORT_CNT = 6,
	CHAN_PER_PORT_CNT = 8,
	PAD_CNT = PORT_CNT * CHAN_PER_PORT_CNT,
	FRAME_BUFFER_SIZE = 3,
};

enum Pins {
	PIN_MULTIPLEX_A = 2,
	PIN_MULTIPLEX_B = 3,
	PIN_MULTIPLEX_C = 4,

	PIN_SOFTSERIAL_RX = 5,
	PIN_SOFTSERIAL_TX = 6,
};


//=================================================================================
// Set Bit and Clwear Bit Helpers
//=================================================================================
#ifndef cbi
#define cbi(sfr, bit) (_SFR_BYTE(sfr) &= ~_BV(bit))
#endif
#ifndef sbi
#define sbi(sfr, bit) (_SFR_BYTE(sfr) |= _BV(bit))
#endif


//=================================================================================
// Prescaler
//=================================================================================
// Maximum sampling frequency    // Resolution
enum Prescaler {
	Prescaler_2 = B00000000, // 16 MHz / 2 = 8 MHz            //
	Prescaler_4 = B00000010, // 16 MHz / 4 = 4 MHz            // ~5.9
	Prescaler_8 = B00000011, // 16 MHz / 8 = 2 MHz            // ~7.4
	Prescaler_16 = B00000100, // 16 MHz / 16 = 1 MHz           // ~8.6
	Prescaler_32 = B00000101, // 16 MHz / 32 = 500 kHz         // ~8.9
	Prescaler_64 = B00000110, // 16 MHz / 64 = 250 kHz         // ~9.0
	Prescaler_128 = B00000111, // 16 MHz / 128 = 125 kHz        // ~9.1
};

inline void setPrescaler(int prescaler) {
	ADCSRA &= B11111000;
	ADCSRA |= prescaler;
}


//=================================================================================
//  Ad Pin
//=================================================================================
enum AdPin {
	AdPin_0 = B00000000,
	AdPin_1 = B00000001,
	AdPin_2 = B00000010,
	AdPin_3 = B00000011,
	AdPin_4 = B00000100,
	AdPin_5 = B00000101,
	AdPin_6 = B00000110, // Bei Atmega8 nur in der Geh?usebauform TQFP und MLF verf?gbar, nicht in PDIP
	AdPin_7 = B00000111, // Bei Atmega8 nur in der Geh?usebauform TQFP und MLF verf?gbar, nicht in PDIP
	AdPin_Vbg = B00001110, // 1.23V
	AdPin_GND = B00001111, // 0V
};

inline void setAdPin(int adPin) {
	ADMUX &= B11110000;
	ADMUX |= adPin;
}

//=================================================================================
// ADC Alignment
//=================================================================================
// Das Ergebnis wird in den Registern ADCH/ADCL linksb?ndig ausgerichtet.
// Die 8 h?chstwertigen Bits des Ergebnisses werden in ADCH abgelegt.
// Die verbleibenden 2 niederwertigen Bits werden im Register ADCL in den Bits 6 und 7 abgelegt.
enum AdcAlignment {
	ADAlignmentLeft = B00100000,
	ADAlignmentRight = B00000000,
};


inline void setADAlignment(int align) {
	ADMUX &= ~B00100000;
	ADMUX |= align;
}

//=================================================================================
inline void startADCConversion() {
	ADCSRA |= B01000000;
}

//=================================================================================

inline void disableAnalogComparator() {
	ACSR = B10000000;
}

inline void multiplexSelectChan(uint8_t chan) {
	PORTD = B00011100 & (chan << 2) | (B11100011 & PORTD);
}

//=================================================================================
// MIDI
//=================================================================================
namespace midi {
	/// http://www.midi.org/techspecs/midimessages.php
#if 1
	struct SysexFrame {
		byte begin = 0xf0;
		byte manufacturer = 42;
		byte msgType = 0;
		unsigned long time1 = 0;
		byte values[PAD_CNT] = { 0 };
		byte end = 0xF7;
	};
#endif

	/**
	Note Off event.
	This message is sent when a note is released (ended).
	*/
	template<typename SERIAL_IF>
	void noteOn(SERIAL_IF& serial, uint8_t note, uint8_t velocity) {
		serial.write((uint8_t)0x90);
		serial.write((uint8_t)note);
		serial.write((uint8_t)velocity);
	}

	/**
	Note On event.
	This message is sent when a note is depressed (start).
	*/
	template<typename SERIAL_IF>
	void noteOff(SERIAL_IF& serial, uint8_t note, uint8_t velocity) {
		serial.write((uint8_t)0x80);
		serial.write((uint8_t)note);
		serial.write((uint8_t)velocity);
	}

	/**
	Polyphonic Key Pressure (Aftertouch).
	This message is most often sent by pressing down on the key after it "bottoms out".
	*/
	template<typename SERIAL_IF>
	void polyphonicKeyPressure(SERIAL_IF& serial, uint8_t note, uint8_t pressure) {
		serial.write((uint8_t)0xA0);
		serial.write((uint8_t)note);
		serial.write((uint8_t)pressure);
	}

	/**
	Control Change.
	This message is sent when a controller value changes.
	Controllers include devices such as pedals and levers.
	Controller numbers 120-127 are reserved as "Channel Mode Messages" (below).
	*/
	template<typename SERIAL_IF>
	void controlChange(SERIAL_IF& serial, uint8_t controllerNumber, uint8_t controllerValue) {
		serial.write((uint8_t)0xB0);
		serial.write((uint8_t)controllerNumber);
		serial.write((uint8_t)controllerValue);
	}
}



//=================================================================================
//
//=================================================================================
struct Configuration {
	enum Type {
		TypeDisabled,
		TypePiezo,
	} type[PAD_CNT] = { TypePiezo };

	struct CurveSettings {
		enum CurveType {
			CurveNormal,
			CurveExp,
			CurveLog,
			CurveSigma,
			CurveFlat,
			CurveExtra,
		};

		CurveType type = CurveNormal;
		uint8_t value = 127;
		int8_t offset = 0;
		uint8_t factor = 127;
	} curve[PAD_CNT];

	uint8_t note[PAD_CNT] = { 0 };
	uint8_t threshold[PAD_CNT] = { 25 };
	uint8_t scanTime[PAD_CNT] = { 25 };
	uint8_t maskTime[PAD_CNT] = { 35 };

} g_configuration;


//=================================================================================
//
//=================================================================================
struct Runtime {
	SoftwareSerial softSerial{ PIN_SOFTSERIAL_RX, PIN_SOFTSERIAL_TX }; // RX, TX

	uint8_t value[PAD_CNT][FRAME_BUFFER_SIZE];

	enum State {
		StateAwait,
		StateScan,
		StateMask,
	} state[PAD_CNT] = { StateAwait };

	uint8_t  trigger[PAD_CNT] = { 0 };
	uint8_t max[PAD_CNT] = { 0 };
	//uint64_t sum[PAD_CNT] = { 0 };

	uint64_t frameCounter = 0;
#if USE_DISPLAY
	bool displayTriggerEvent[PAD_CNT] = { 0 };
#endif
} g_runtime;


//=================================================================================
//
//=================================================================================
inline uint8_t calcCurve(const Configuration::CurveSettings& curveSettings, uint8_t value) {
	uint8_t ret = 0;

	float x = value * 8.0;
	float f = ((float)curveSettings.value) / 64.0; //[1;127]->[0.;2.0]

	switch(curveSettings.type) {
		//[0-1023]x[0-127]
		case Configuration::CurveSettings::CurveNormal:
			ret = x * f / 16.0;
			break;

		case Configuration::CurveSettings::CurveExp:
			ret = (127.0 / (exp(2.0 * f) - 1)) * (exp(f * x / 512.0) - 1.0);
			break; //Exp 4*(exp(x/256)-1)

		case Configuration::CurveSettings::CurveLog:
			ret = log(1.0 + (f * x / 128.0)) * (127.0 / log((8 * f) + 1));
			break; //Log 64*log(1+x/128)

		case Configuration::CurveSettings::CurveSigma:
			ret = (127.0 / (1.0 + exp(f * (512.0 - x) / 64.0)));
			break; //Sigma

		case Configuration::CurveSettings::CurveFlat:
			ret = (64.0 - ((8.0 / f) * log((1024 / (1 + x)) - 1)));
			break; //Flat

		case Configuration::CurveSettings::CurveExtra:
			ret = (x + 0x20) * f / 16.0;

	}

	ret = ret * (curveSettings.factor / 127.0) + curveSettings.offset;

	if(ret <= 0) {
		return 0;
	}

	if(ret >= 127) {
		return 127;    //127
	}

	return ret;
}


//=================================================================================
//
//=================================================================================
void setup() {
#if USE_DISPLAY
	lcd.begin(16, 2);
	delay(500);
	lcd.print("Drumduino  0.0.1");
	delay(1000);
#endif


	memset(g_runtime.value, 0, sizeof(g_runtime.value));

	// generate note mapping
	for(uint8_t pad = 0; pad < PAD_CNT; ++pad) {
		uint8_t note = 0x1E + pad;
		g_configuration.note[pad] = note;
	}

	// Setup MultiplexSelection Pins
	pinMode(PIN_MULTIPLEX_A, OUTPUT);
	pinMode(PIN_MULTIPLEX_B, OUTPUT);
	pinMode(PIN_MULTIPLEX_C, OUTPUT);

	// Setup ADCs
	analogReference(DEFAULT);
	disableAnalogComparator();
	setPrescaler(Prescaler_8);
	//setADAlignment(ADAlignmentLeft);

	// Disable digital input buffers on all analog input pins
	DIDR0 = DIDR0 | B00111111;

	// Setup Serial
	Serial.begin(2000000);
	Serial.flush();

	g_runtime.softSerial.begin(31250);
	//g_runtime.softSerial.flush();
}


//=================================================================================
//
//=================================================================================
void loop() {
	midi::SysexFrame sysexFrame;

	uint64_t& frameCounter = g_runtime.frameCounter;
	size_t curFrameIdx = frameCounter % FRAME_BUFFER_SIZE;
	size_t lastFrameIdx = (frameCounter - 1) % FRAME_BUFFER_SIZE;

	for(uint8_t chan = 0; chan < CHAN_PER_PORT_CNT; ++chan) {
		multiplexSelectChan(chan);

		for(uint8_t port = 0; port < PORT_CNT; ++port) {
			int pad = port * CHAN_PER_PORT_CNT + chan;

			// shortcuts!
			uint8_t& currentValue = g_runtime.value[pad][curFrameIdx];
			const uint8_t& lastValue = g_runtime.value[pad][lastFrameIdx];

			Runtime::State& state = g_runtime.state[pad];
			uint8_t& triggerFrame = g_runtime.trigger[pad];
			uint8_t& maxValue = g_runtime.max[pad];
			//const uint8_t& sumValue = g_runtime.sum[pad];

			const Configuration::Type& type = g_configuration.type[pad];
			const uint8_t& threshold = g_configuration.threshold[pad];
			const uint8_t& scanTime = g_configuration.scanTime[pad];
			const uint8_t& maskTime = g_configuration.maskTime[pad];

			// real processing
			currentValue = uint8_t(analogRead(port) >> 3);

			switch(type) {
				case Configuration::TypePiezo: {
					switch(state) {
						// In this state we wait for a signal to trigger
						default:
						case Runtime::StateAwait: {
STATE_AGAIN:

							if(currentValue < lastValue + threshold) {
								break;
							}

							state = Runtime::StateScan;
							triggerFrame = frameCounter;
							maxValue = currentValue;
							//sumValue = currentValue;
							//### fallthrough
						}

						// In this state we measure the value for the given time period to get the max value
						case Runtime::StateScan: {
							if(frameCounter < triggerFrame + scanTime) {
								maxValue = max(currentValue, maxValue);
								//sumValue += currentValue;
								break;
							}

							const Configuration::CurveSettings& curve = g_configuration.curve[pad];
							uint8_t velocity = calcCurve(curve, maxValue);

							const uint8_t& note = g_configuration.note[pad];
							midi::noteOn(g_runtime.softSerial, note, velocity);
							state = Runtime::StateMask;
#if USE_DISPLAY
							g_runtime.displayTriggerEvent[pad] = true;
#endif
							//### fallthrough
						}

						// In this state we do nothing to prevent retriggering
						case Runtime::StateMask: {
							if(frameCounter < triggerFrame + scanTime + maskTime) {
								break;
							}

							state = Runtime::StateAwait;
							//goto STATE_AGAIN;
						}
					}
				}
			}
		}
	}

#if USE_DISPLAY

	if(frameCounter % 1000 == 0) {
		lcd.clear();

		lcd.setCursor(0, 0);

		switch(g_configuration.type[0]) {
			default:
			case Configuration::TypeDisabled: {
				lcd.print("Off");
				break;
			}

			case Configuration::TypePiezo: {
				lcd.print("Piez");
				break;
			}
		}

		lcd.setCursor(5, 0);
		lcd.print(g_configuration.note[0]);
		lcd.setCursor(9, 0);
		lcd.print(g_configuration.scanTime[0]);
		lcd.setCursor(13, 0);
		lcd.print(g_configuration.threshold[0]);


		lcd.setCursor(0, 1);
		lcd.print("CurV:");
		lcd.setCursor(6, 1);
		lcd.print(g_runtime.value[0][curFrameIdx]);

		lcd.setCursor(11, 1);

		switch(g_runtime.state[0]) {
			default:
			case Runtime::StateAwait: {
				lcd.print("A");
				break;
			}

			case Runtime::StateScan: {
				lcd.print("S");
				break;
			}

			case Runtime::StateMask: {
				lcd.print("M");
				break;
			}
		}

		lcd.setCursor(13, 1);

		if(g_runtime.displayTriggerEvent[0]) {

			lcd.print("[x]");
		}
		else {
			lcd.print("[ ]");
		}
	}

	if(frameCounter % 1000 == 0) {
		memset(g_runtime.displayTriggerEvent, 0, sizeof(g_runtime.displayTriggerEvent));
	}

#endif
	sysexFrame.time1 = millis();
	for(int pad = 0; pad < PAD_CNT; ++pad) {
		sysexFrame.values[pad] = g_runtime.value[pad][curFrameIdx];
	}


	Serial.write((const char*)&sysexFrame, sizeof(sysexFrame));

	++frameCounter;
}
